// Logisim project Lab 3 Final.circ as structural Verilog: 1 circuit, main circuit main
module main (
  input  S0,
  input  S1,
  input  A1,
  input  B1,
  input  A2,
  input  B2,
  input  A3,
  input  B3,
  input  A4,
  input  B4
);

  wire adder_1_cout, adder_1_out, adder_2_cout, adder_2_out, adder_3_cout, adder_3_out, adder_4_out,
       nor_1_out, nor_2_out, nor_3_out, nor_4_out, not_1_out, not_2_out, not_3_out, not_4_out, xnor_1_out,
       xor_1_out, xor_2_out, xor_3_out, xor_4_out, xor_5_out;

  xnor xnor_1 (xnor_1_out, S0, S1);
  xor xor_1 (xor_1_out, xnor_1_out, S1);
  not not_1 (not_1_out, B1);
  not not_2 (not_2_out, B2);
  not not_3 (not_3_out, B3);
  not not_4 (not_4_out, B4);
  nor nor_1 (nor_1_out, xnor_1_out, not_1_out);
  nor nor_2 (nor_2_out, xnor_1_out, not_2_out);
  nor nor_3 (nor_3_out, xnor_1_out, not_3_out);
  nor nor_4 (nor_4_out, xnor_1_out, not_4_out);
  xor xor_2 (xor_2_out, nor_1_out, S1);
  xor xor_3 (xor_3_out, nor_2_out, S1);
  xor xor_4 (xor_4_out, nor_3_out, S1);
  xor xor_5 (xor_5_out, nor_4_out, S1);
  Adder #(.width(1)) adder_1 (.a(A1), .b(xor_2_out), .out(adder_1_out), .cin(xor_1_out), .cout(adder_1_cout));
  Adder #(.width(1)) adder_2 (.a(A2), .b(xor_3_out), .out(adder_2_out), .cin(adder_1_cout), .cout(adder_2_cout));
  Adder #(.width(1)) adder_3 (.a(A3), .b(xor_4_out), .out(adder_3_out), .cin(adder_2_cout), .cout(adder_3_cout));
  Adder #(.width(1)) adder_4 (.a(A4), .b(xor_5_out), .out(adder_4_out), .cin(adder_3_cout));  // open: cout
  LED led_1 (.in(adder_4_out));
  LED led_2 (.in(adder_3_out));
  LED led_3 (.in(adder_2_out));
  LED led_4 (.in(adder_1_out));

  // Notes on the sheet:
  //   8
  //   4
  //   2
  //   1
endmodule
