// Logisim project Lab 4 - Multiplexers.circ as structural Verilog: 1 circuit, main circuit main
module main (
  input  _7,
  input  _6,
  input  _5,
  input  _4,
  input  _3,
  input  _2,
  input  _1,
  input  _0,
  input  [2:0] X,
  input  _3_2,
  input  Z,
  input  Z_2,
  input  _0_2,
  input  [1:0] X_2
);

  wire multiplexer_1_out, multiplexer_2_out;

  Multiplexer #(.select(3)) multiplexer_1 (
    .in0(_0), .in1(_1), .in2(_2), .in3(_3), .in4(_4), .in5(_5), .in6(_6), .in7(_7), .out(multiplexer_1_out),
    .sel(X));  // open: en
  Multiplexer #(.select(2)) multiplexer_2 (
    .in0(_0_2), .in1(Z_2), .in2(Z), .in3(_3_2), .out(multiplexer_2_out), .sel(X_2));  // open: en
  LED led_1 (.in(multiplexer_1_out));
  LED led_2 (.in(multiplexer_2_out));

  // Notes on the sheet:
  //   PART A
  //   PART B
  //   Y
  //   Y
  //   Z
endmodule
