// Logisim project Lab5 - Sequential Circuits.circ as structural Verilog: 1 circuit, main circuit main
module main (
  input  in_1,
  input  in_2,
  input  in_3,
  input  in_4,
  input  in_5,
  input  in_6,
  input  in_7
);

  wire and_1_out, and_2_out, clock_1_out, clock_2_out, clock_3_out, clock_4_out, d_ff_1_q, d_ff_1_qn,
       d_ff_2_q, d_ff_2_qn, j_k_ff_1_q, j_k_ff_1_qn, j_k_ff_2_q, j_k_ff_2_qn, nor_1_out, nor_2_out,
       not_1_out, not_2_out, not_3_out, not_4_out, xor_1_out, xor_2_out;

  Clock clock_1 (.out(clock_1_out));
  Clock clock_2 (.out(clock_2_out));
  not not_1 (not_1_out, in_4);
  not not_2 (not_2_out, in_6);
  not not_3 (not_3_out, in_7);
  LED led_1 (.in(j_k_ff_1_q));
  J_K_Flip_Flop j_k_ff_1 (
    .J(in_1), .clk(clock_1_out), .K(in_3), .Q(j_k_ff_1_q), .Qn(j_k_ff_1_qn));  // open: preset, en, reset
  LED led_2 (.in(j_k_ff_1_qn));
  LED led_3 (.in(j_k_ff_2_q));
  J_K_Flip_Flop j_k_ff_2 (
    .J(in_4), .clk(clock_2_out), .K(not_1_out), .Q(j_k_ff_2_q), .Qn(j_k_ff_2_qn));  // open: preset, en, reset
  LED led_4 (.in(j_k_ff_2_qn));
  xor xor_1 (xor_1_out, not_2_out, not_3_out);
  and and_1 (and_1_out, not_2_out, xor_1_out);
  and and_2 (and_2_out, xor_1_out, not_3_out);
  LED led_5 (.in(nor_1_out));
  nor nor_1 (nor_1_out, and_1_out, nor_2_out);
  LED led_6 (.in(nor_2_out));
  nor nor_2 (nor_2_out, nor_1_out, and_2_out);
  Clock clock_3 (.out(clock_3_out));
  Clock clock_4 (.out(clock_4_out));
  xor xor_2 (xor_2_out, d_ff_2_qn, not_4_out);
  D_Flip_Flop d_ff_1 (.clk(clock_3_out), .D(in_2), .Q(d_ff_1_q), .Qn(d_ff_1_qn));  // open: preset, en, reset
  LED led_7 (.in(d_ff_1_q));
  LED led_8 (.in(d_ff_1_qn));
  LED led_9 (.in(d_ff_2_q));
  D_Flip_Flop d_ff_2 (.clk(clock_4_out), .D(xor_2_out), .Q(d_ff_2_q), .Qn(d_ff_2_qn));  // open: preset, en, reset
  LED led_10 (.in(d_ff_2_qn));
  not not_4 (not_4_out, in_5);

  // Notes on the sheet:
  //   Part A
  //   J/K Flip-Flop
  //   Part C
  //   J/K as D Flip-Flop
  //   Part E
  //   Modified SR Flip-Flop
  //   D Flip-Flop
  //   Part D
  //   D as T Flip-FLop
  //   Part B
endmodule
