// Logisim project Shift Register.circ as structural Verilog: 1 circuit, main circuit main
module main (
  input  Serial_in,
  input  Serial_in_2,
  input  Clear,
  input  Load,
  input  Load_2,
  input  Load_3,
  input  Load_All,
  input  [3:0] in_8,
  input  Allow_Shift,
  input  Serial_in_3,
  input  Clear_All,
  input  Allow_Rotate,
  output [3:0] Out
);

  wire and_1_out, and_2_out, clock_1_out, clock_2_out, clock_3_out, d_ff_1_q, d_ff_2_q, d_ff_3_q, d_ff_4_q,
       d_ff_5_q, d_ff_6_q, d_ff_7_q, d_ff_8_q, d_ff_9_q, shift_register_1_out, xor_1_out;

  Clock clock_1 (.out(clock_1_out));
  D_Flip_Flop d_ff_1 (.clk(clock_1_out), .D(Serial_in), .Q(d_ff_1_q));  // open: Qn, preset, en, reset
  D_Flip_Flop d_ff_2 (.clk(clock_1_out), .D(d_ff_1_q), .Q(d_ff_2_q), .reset(Clear));  // open: Qn, preset, en
  D_Flip_Flop d_ff_3 (.clk(clock_1_out), .D(d_ff_2_q), .Q(d_ff_3_q), .preset(Load));  // open: Qn, en, reset
  xor xor_1 (xor_1_out, Serial_in_3, and_1_out);
  Clock clock_2 (.out(clock_2_out));
  D_Flip_Flop d_ff_4 (.clk(clock_1_out), .D(d_ff_3_q), .Q(d_ff_4_q));  // open: Qn, preset, en, reset
  Shift_Register #(.length(4)) shift_register_1 (
    .shift(Allow_Shift), .in(xor_1_out), .clk(clock_2_out), .out(shift_register_1_out), .load(Load_All),
    .clr(Clear_All), .d0(in_8[3]), .q0(Out[3]), .d1(in_8[2]), .q1(Out[2]), .d2(in_8[1]), .q2(Out[1]),
    .d3(in_8[0]), .q3(Out[0]));
  LED led_1 (.in(d_ff_4_q));
  LED led_2 (.in(shift_register_1_out));
  and and_1 (and_1_out, shift_register_1_out, Allow_Rotate);
  Clock clock_3 (.out(clock_3_out));
  D_Flip_Flop d_ff_5 (.clk(clock_3_out), .D(Serial_in_2), .Q(d_ff_5_q));  // open: Qn, preset, en, reset
  D_Flip_Flop d_ff_6 (.clk(clock_3_out), .D(d_ff_5_q), .Q(d_ff_6_q), .preset(d_ff_7_q));  // open: Qn, en, reset
  D_Flip_Flop d_ff_7 (.clk(clock_3_out), .D(Load_2), .Q(d_ff_7_q));  // open: Qn, preset, en, reset
  D_Flip_Flop d_ff_8 (.clk(clock_3_out), .D(d_ff_6_q), .Q(d_ff_8_q), .preset(and_2_out));  // open: Qn, en, reset
  and and_2 (and_2_out, Load_3, clock_3_out);
  D_Flip_Flop d_ff_9 (.clk(clock_3_out), .D(d_ff_8_q), .Q(d_ff_9_q));  // open: Qn, preset, en, reset
  LED led_3 (.in(d_ff_9_q));

  // Notes on the sheet:
  //   Part A
  //   4-bit Shift Register
  //   Part B
  //   Serial out
  //   Serial out
  //   Rising edge
  //   #2?
  //   Part A
  //   Modified Load 4-bit Shift Register
  //   #1?
  //   Serial out
endmodule
