// Logisim project Counter.circ as structural Verilog: 1 circuit, main circuit main
module main (
);

  wire and_1_out, and_2_out, and_3_out, and_4_out, and_5_out, and_6_out, and_7_out, and_8_out, and_9_out,
       and_10_out, clock_1_out, j_k_ff_1_q, j_k_ff_2_q, j_k_ff_3_q, j_k_ff_4_q, not_1_out, not_2_out,
       not_3_out, not_4_out, not_5_out, not_6_out, not_7_out, not_8_out, not_9_out, not_10_out, not_11_out,
       not_12_out, not_13_out, not_14_out, not_15_out, or_1_out, or_2_out, or_3_out, or_4_out;

  not not_1 (not_1_out, j_k_ff_2_q);
  not not_2 (not_2_out, j_k_ff_3_q);
  not not_3 (not_3_out, j_k_ff_3_q);
  not not_4 (not_4_out, j_k_ff_1_q);
  not not_5 (not_5_out, j_k_ff_2_q);
  not not_6 (not_6_out, j_k_ff_4_q);
  not not_7 (not_7_out, j_k_ff_1_q);
  not not_8 (not_8_out, j_k_ff_4_q);
  not not_9 (not_9_out, j_k_ff_3_q);
  not not_10 (not_10_out, j_k_ff_4_q);
  not not_11 (not_11_out, j_k_ff_1_q);
  and and_1 (and_1_out, j_k_ff_1_q, j_k_ff_4_q);
  and and_2 (and_2_out, not_1_out, not_2_out);
  and and_3 (and_3_out, not_3_out, j_k_ff_4_q);
  and and_4 (and_4_out, not_4_out, not_5_out);
  and and_5 (and_5_out, j_k_ff_3_q, not_6_out);
  and and_6 (and_6_out, not_7_out, not_8_out);
  and and_7 (and_7_out, j_k_ff_1_q, j_k_ff_3_q);
  and and_8 (and_8_out, j_k_ff_2_q, j_k_ff_3_q, j_k_ff_4_q);
  and and_9 (and_9_out, not_9_out, not_10_out);
  and and_10 (and_10_out, not_11_out, j_k_ff_4_q);
  or or_1 (or_1_out, and_1_out, and_2_out, and_3_out);
  not not_12 (not_12_out, or_1_out);
  or or_2 (or_2_out, and_4_out, and_5_out, and_6_out);
  not not_13 (not_13_out, or_2_out);
  or or_3 (or_3_out, and_7_out, and_8_out, and_9_out);
  not not_14 (not_14_out, or_3_out);
  or or_4 (or_4_out, and_9_out, and_10_out);
  not not_15 (not_15_out, or_4_out);
  J_K_Flip_Flop j_k_ff_1 (
    .J(or_1_out), .clk(clock_1_out), .K(not_12_out), .Q(j_k_ff_1_q));  // open: Qn, preset, en, reset
  J_K_Flip_Flop j_k_ff_2 (
    .J(or_2_out), .clk(clock_1_out), .K(not_13_out), .Q(j_k_ff_2_q));  // open: Qn, preset, en, reset
  Clock clock_1 (.out(clock_1_out));
  J_K_Flip_Flop j_k_ff_3 (
    .J(or_3_out), .clk(clock_1_out), .K(not_14_out), .Q(j_k_ff_3_q));  // open: Qn, preset, en, reset
  J_K_Flip_Flop j_k_ff_4 (
    .J(or_4_out), .clk(clock_1_out), .K(not_15_out), .Q(j_k_ff_4_q));  // open: Qn, preset, en, reset
  LED led_1 (.in(j_k_ff_1_q));
  LED led_2 (.in(j_k_ff_2_q));
  LED led_3 (.in(j_k_ff_3_q));
  LED led_4 (.in(j_k_ff_4_q));

  // Notes on the sheet:
  //   AD
  //   B'C'
  //   C'D
  //   A'B'
  //   CD'
  //   A'D'
  //   AC
  //   BCD
  //   C'D'
  //   A'D
  //   A
  //   B
  //   C
  //   D
endmodule
